# Fritzing sketch sistema_controle_alarme (saved by Fritzing 0.9.2b)
breadboards: 1

parts:
  Componente1 = Arduino Uno (Rev3)
  J1 = Piezo Speaker
  LED1 = LED - 5mm [color="Red (633nm)" package="5 mm [THT]"]
  R1 = Resistor [tolerance=±5% resistance=10k package=THT]
  S3 = Pushbutton [package=THT]
  M1 = DC Motor

nets:
  N1: Componente1.D10_PWM/SS, R1.Pin_1
  N2: Componente1.D11_PWM/MOSI, M1.pin_2
  N3: Componente1.D2, S3.leg1
  N4: Componente1.GND, J1.pin2, LED1.anode, S3.leg0, M1.pin_1
  N5: LED1.cathode, R1.Pin_0

notes:
  Modulo Bluetooth

// code stored in the sketch: Sistema_para_controle_de_alarme_arduino.ino
/*-------------------------------------------------------
  Prototipo Projeto Iniciação cientifica 2015-2 á 2016-2
  Representação maquina de estados que sera controlada
  pela cadeirinha inteligente, essa maquina de estados
  controla ao dispositivo ligado a chave do motorista.
  Temos como entrada a comunicação, presença da criança
  e o botao de consciencia, e como saidas temos um led,
  um vibrador e um buzzer. 
--------------------------------------------------------
*/
#include<SoftwareSerial.h>

int bluetoothTx = 3;
int bluetoothRx = 4;

SoftwareSerial bluetooth(bluetoothTx,bluetoothRx);

//Sinais
int led_1=10,
    led_2=11,
    led_3=12,
    pin_butt = 2;
  
//sinais para teste 
  int butt2=3,
      butt3=4;
    
//entradas
int comm,
    cri,
    butt;

//configuração inicial
void setup()
{
  Serial.begin(9600);
  /*
  bluetooth.begin(115200);
  delay(100);
  bluetooth.println("U,9600,N");
  bluetooth.begin(9600);
 */
  pinMode(led_1,OUTPUT);
  pinMode(led_2,OUTPUT);
  pinMode(led_3,OUTPUT);
  pinMode(pin_butt,INPUT);
  
  //pinagem para testes
  pinMode(butt2,INPUT);
  pinMode(butt3,INPUT);
}

//Loop de execução do codigo
void loop()
{
  /*
  // Define as entradas comunicação e criança
  if(bluetooth.available()){
    comm=1;
    cri = mapeamento((char)bluetooth.read());
  }else{
    comm=0;
  }
  */
  
  //entradas teste para comm e cri
  comm=digitalRead(butt2);
  cri = digitalRead(butt3);
  
  //Entrada do botao de consciencia
  if(digitalRead(pin_butt)==HIGH){
    butt = 1;
  }else{
     butt=0; 
  }
  
  int* vet=maquina_estados(comm, cri, butt);
  
  //controle sinal visual
  if(vet[0]==1){
    tone(led_1,5);  //tone(pino, frequencia); 
  }else{
    digitalWrite(led_1,LOW);
  }
  
  //controle do sinal vibratorio 
  digitalWrite(12,vet[1]);
  
   //controle do sinal sonoro
  if(vet[2]==1){
    tone(led_3,262);
  }else{
    noTone(led_3);
  }

  free(vet);  
}

//Maquina de Estados do projeto
int * maquina_estados(int communication, int crianca, int button)
{
//estados
const int WAIT=0,
          STAND_BY=1,
          LED=2,
          LED_VIBRA1=3,
          LED_VIBRA2=4,
          LED_VIBRA_APITA=5;
          
//estado atual
static int state=0;

  int * saida=(int *)calloc(3,sizeof(int));
  
  switch(state)
  {
    case WAIT :
          if(communication==0 && crianca==0)
          {
	      state=STAND_BY;
	      saida[0]=0;
              saida[1]=0;
              saida[2]=0;
          }else if(communication==0 && crianca==1)
	        {
                  state=LED;
	          saida[0]=1;
                  saida[1]=0;
                  saida[2]=0;
                }else
                {
                  state=WAIT;
                  saida[0]=0;
                  saida[1]=0;
                  saida[2]=0;
                }
	break;
     case STAND_BY :
            if(communication==1)
            {  
		state=WAIT;
		saida[0]=0;
                saida[1]=0;
                saida[2]=0;
	    }
         break;
      case LED : 
            if(crianca==0 && communication==1)
            {
		state=WAIT;
		saida[0]=0;
                saida[1]=0;
                saida[2]=0;
            }else if(button==1)
                  {
                    //tempo 4
                    delay(300);
                    state=LED_VIBRA2;
		    saida[0]=1;
                    saida[1]=1;
                    saida[2]=0;
                  }else
                  {
                    //TEMPO 1
                    delay(300);
                    state=LED_VIBRA1;
		    saida[0]=1;
                    saida[1]=1;
                    saida[2]=0;
	          }
         break;
       case LED_VIBRA1 :
             if(crianca==0 && communication==1)
             {
               state=WAIT;
	       saida[0]=0;
               saida[1]=0;
               saida[2]=0;
             }else if(button==1)
                    {
                      state=LED_VIBRA2;
		     saida[0]=1;
                     saida[1]=1;
                     saida[2]=0;
                    } else
                      {
                        //TEMPO 2
                        delay(300);
                        state=LED_VIBRA_APITA;
                        saida[0]=1;
                        saida[1]=1;
                        saida[2]=1;
                      }
           break;
	case LED_VIBRA_APITA :
              if(crianca==0 && communication==1)
              {
                state=WAIT;
		saida[0]=0;
                saida[1]=0;
                saida[2]=0;
              } else if(button==1)
                      {
                        state=LED_VIBRA2;
			saida[0]=1;
                        saida[1]=1;
                        saida[2]=0;
		      }else
                        {
                          state=LED_VIBRA_APITA;
			  saida[0]=1;
                          saida[1]=1;
                          saida[2]=1;
			}
          break;
	case LED_VIBRA2	:
              if(crianca==0 && communication==1)
              {
                state=WAIT;
		saida[0]=0;
                saida[1]=0;
                saida[2]=0;
	      }else
                {
                  //TEMPO 3
                  delay(300);
                  state=LED_VIBRA_APITA;
		  saida[0]=1;
                  saida[1]=1;
                  saida[2]=1;
                }
           break;
         default : 
             state=WAIT;
	     saida[0]=0;
             saida[1]=0;
             saida[2]=0;
          break;
  }
  return saida;
}

//Realiza o mapeamento entre String para inteiro 
int mapeamento(char valor){
  switch(valor){
   case 'p':
      return 1;
     break;
    case 'a':
     return 0; 
  }
}
